# Fritzing sketch signal_breakout (saved by Fritzing 0.9.3b)
perfboards: 1

parts:
  ESC = polarizedheader 4pin 0.156in [package=THT]
  SERVO2 = Header 3 [package=molex-1x3_lock]
  SERVO1 = Header 3 [package=molex-1x3_lock]
  SIG_OUT = polarizedheader 4pin 0.156in [package=THT]
  SERVO3 = Header 3 [package=molex-1x3_lock]

nets:
  N1: ESC.pin1, SERVO2.3, SERVO1.3, SERVO3.3
  N2: ESC.pin2, SERVO2.2, SERVO1.2, SERVO3.2
  N3: ESC.pin3, SIG_OUT.pin1
  N4: SERVO2.1, SIG_OUT.pin3
  N5: SERVO1.1, SIG_OUT.pin4
  N6: SIG_OUT.pin2, SERVO3.1
